// Logisim project operaciones-aritmeticas-suma.circ as structural Verilog: 1 circuit, main circuit main
module main (
  input  [3:0] in_1,
  input  [3:0] in_2,
  output [4:0] out_3
);

  wire adder_1_cout;
  wire [3:0] adder_1_out;

  Adder #(.width(4)) adder_1 (.a(in_1), .b(in_2), .out(adder_1_out), .cout(adder_1_cout));  // open: cin
  assign out_3 = {{1{adder_1_cout}}, adder_1_out};  // Bit_Extender bit_extender_1
endmodule
