// Logisim project suma-resta-complemento2-comparador.circ as structural Verilog: 1 circuit, main circuit main
module main (
  input  [3:0] x,
  input  [3:0] y
);

  wire comparator_1_eq, comparator_1_gt, comparator_1_lt;
  wire [3:0] adder_1_out, negator_1_out, subtractor_1_out;

  Negator #(.width(4)) negator_1 (.in(y), .out(negator_1_out));
  // Probe on subtractor_1_out
  Subtractor #(.width(4)) subtractor_1 (.a(x), .b(y), .out(subtractor_1_out));  // open: bin, bout
  Adder #(.width(4)) adder_1 (.a(x), .b(negator_1_out), .out(adder_1_out));  // open: cin, cout
  // Probe on adder_1_out
  Comparator #(.width(4)) comparator_1 (
    .a(subtractor_1_out), .b(adder_1_out), .gt(comparator_1_gt), .eq(comparator_1_eq), .lt(comparator_1_lt));
  LED led_1 (.in(comparator_1_gt));
  LED led_2 (.in(comparator_1_eq));
  LED led_3 (.in(comparator_1_lt));
endmodule
